// Logisim project SAP_1.circ as structural Verilog: 1 circuit, main circuit main
module main (
  input  A,
  input  B,
  input  C,
  output out_4
);

  wire and_1_out, and_2_out;

  and and_1 (and_1_out, ~A, ~C);  // AND_Gate
  and and_2 (and_2_out, B, C);
  or or_1 (out_4, and_1_out, and_2_out);

  // Notes on the sheet:
  //   S= (A'.C') + (B.C)
endmodule
